// Logisim project projet secret.circ as structural Verilog: 1 circuit, main circuit main
module main (
  input  in_1,
  input  in_2,
  input  in_3,
  input  in_4,
  input  in_5,
  input  in_6,
  output out_7,
  output out_8,
  output out_9,
  output out_10,
  output out_11,
  output out_12,
  output out_13,
  output out_14,
  output out_15,
  output out_16,
  output out_17,
  output out_18,
  output out_19
);

  wire and_1_out, and_2_out, and_3_out, and_5_out, and_6_out, and_8_out, and_9_out, not_1_out, not_2_out,
       not_3_out, or_1_out, or_2_out, or_5_out, xor_1_out, xor_2_out, xor_3_out, xor_5_out;

  and and_1 (and_1_out, in_1, in_2);
  xor xor_1 (xor_1_out, in_2, in_3);
  not not_1 (not_1_out, in_3);
  and and_2 (and_2_out, in_4, in_5);
  buf or_1 (or_1_out, and_1_out);  // OR_Gate
  xor xor_2 (xor_2_out, in_4, in_6);
  not not_2 (not_2_out, xor_1_out);
  or or_2 (or_2_out, not_1_out, in_5);
  and and_3 (and_3_out, and_1_out, and_2_out);
  // AND_Gate and_4 has open pins: in0=or_1_out, in1=xor_2_out, out=open
  and and_5 (and_5_out, in_5, in_4);
  and and_6 (and_6_out, or_2_out, not_2_out);
  xor xor_3 (xor_3_out, not_2_out, and_3_out);
  // AND_Gate and_7 has open pins: in0=not_2_out, in1=and_3_out, out=open
  not not_3 (not_3_out, and_3_out);
  or or_3 (out_19, and_3_out, and_5_out);
  buf and_8 (and_8_out, and_6_out);  // AND_Gate
  and and_9 (and_9_out, and_6_out, xor_3_out);
  xor xor_4 (out_17, not_3_out, out_19);
  xor xor_5 (xor_5_out, not_2_out, and_8_out);
  buf and_10 (out_10, and_8_out);  // AND_Gate
  or or_4 (out_11, and_9_out, out_17);
  or or_5 (or_5_out, and_8_out, xor_5_out);
  and and_11 (out_13, out_11, not_3_out);
  and and_12 (out_16, not_3_out, xor_3_out);
  not not_4 (out_7, or_5_out);
  xor xor_6 (out_8, or_5_out, out_13);
  and and_13 (out_9, out_10, out_13);
  or or_6 (out_18, out_13, out_19);

  assign out_12 = out_8;
  assign out_14 = out_10;
  assign out_15 = out_11;
endmodule
